# Fritzing sketch monstermega (saved by Fritzing 0.9.4)
circuit board: 45.8799cm x 16.9834cm
breadboards: 3

parts:
  Arduino_Mega_2560_(Rev_3) = Arduino Mega 2560 (Rev3)
  U8 = 74HC595 [package="DIP16 [THT]"]
  U9 = 74HC595 [package="DIP16 [THT]"]
  U10 = 74HC595 [package="DIP16 [THT]"]
  U11 = 74HC595 [package="DIP16 [THT]"]
  U12 = 74HC595 [package="DIP16 [THT]"]
  U13 = 74HC595 [package="DIP16 [THT]"]
  U14 = 74HC595 [package="DIP16 [THT]"]
  U15 = 74HC595 [package="DIP16 [THT]"]
  U16 = 74HC595 [package="DIP16 [THT]"]
  U17 = 74HC595 [package="DIP16 [THT]"]
  U18 = 74HC595 [package="DIP16 [THT]"]
  U19 = 74HC595 [package="DIP16 [THT]"]
  U20 = 74HC595 [package="DIP16 [THT]"]
  U21 = 74HC595 [package="DIP16 [THT]"]
  U22 = 74HC595 [package="DIP16 [THT]"]
  U23 = 74HC595 [package="DIP16 [THT]"]
  U24 = 74HC595 [package="DIP16 [THT]"]
  ATmega_2560_16au = ATMEGA2560 [package=tqfp]
  J41 = female pin header, 2 pins [form="♀ (female)"]  # not connected
  J42 = female pin header, 2 pins [form="♀ (female)"]  # not connected
  J43 = female pin header, 2 pins [form="♀ (female)"]  # not connected
  J44 = female pin header, 2 pins [form="♀ (female)"]  # not connected
  J45 = female pin header, 2 pins [form="♀ (female)"]  # not connected
  J46 = female pin header, 2 pins [form="♀ (female)"]  # not connected
  J47 = female pin header, 2 pins [form="♀ (female)"]  # not connected
  J48 = female pin header, 2 pins [form="♀ (female)"]  # not connected
  J49 = female pin header, 2 pins [form="♀ (female)"]  # not connected
  J50 = female pin header, 2 pins [form="♀ (female)"]  # not connected
  J51 = female pin header, 2 pins [form="♀ (female)"]  # not connected
  J52 = female pin header, 2 pins [form="♀ (female)"]  # not connected
  J53 = female pin header, 2 pins [form="♀ (female)"]  # not connected
  J54 = female pin header, 2 pins [form="♀ (female)"]  # not connected
  J55 = female pin header, 2 pins [form="♀ (female)"]  # not connected
  J56 = female pin header, 2 pins [form="♀ (female)"]  # not connected
  J57 = female pin header, 2 pins [form="♀ (female)"]  # not connected
  J58 = female pin header, 2 pins [form="♀ (female)"]  # not connected
  J59 = female pin header, 2 pins [form="♀ (female)"]  # not connected
  J60 = female pin header, 2 pins [form="♀ (female)"]  # not connected
  J61 = female pin header, 2 pins [form="♀ (female)"]  # not connected
  J62 = female pin header, 2 pins [form="♀ (female)"]  # not connected
  J63 = female pin header, 2 pins [form="♀ (female)"]  # not connected
  J64 = female pin header, 2 pins [form="♀ (female)"]  # not connected
  J65 = female pin header, 2 pins [form="♀ (female)"]  # not connected
  J66 = female pin header, 2 pins [form="♀ (female)"]  # not connected
  J67 = female pin header, 2 pins [form="♀ (female)"]  # not connected
  J68 = female pin header, 2 pins [form="♀ (female)"]  # not connected
  J69 = female pin header, 2 pins [form="♀ (female)"]  # not connected
  J70 = female pin header, 2 pins [form="♀ (female)"]  # not connected
  J71 = female pin header, 2 pins [form="♀ (female)"]  # not connected
  J72 = female pin header, 2 pins [form="♀ (female)"]  # not connected
  J73 = female pin header, 2 pins [form="♀ (female)"]  # not connected
  J74 = female pin header, 2 pins [form="♀ (female)"]  # not connected
  J75 = female pin header, 2 pins [form="♀ (female)"]  # not connected
  J76 = female pin header, 2 pins [form="♀ (female)"]  # not connected
  J77 = female pin header, 2 pins [form="♀ (female)"]  # not connected
  J78 = female pin header, 2 pins [form="♀ (female)"]  # not connected
  J79 = female pin header, 2 pins [form="♀ (female)"]  # not connected
  J80 = female pin header, 2 pins [form="♀ (female)"]  # not connected
  J81 = female pin header, 2 pins [form="♀ (female)"]  # not connected
  J82 = female pin header, 2 pins [form="♀ (female)"]  # not connected
  J83 = female pin header, 2 pins [form="♀ (female)"]  # not connected
  J84 = female pin header, 2 pins [form="♀ (female)"]  # not connected
  J85 = female pin header, 2 pins [form="♀ (female)"]  # not connected
  J86 = female pin header, 2 pins [form="♀ (female)"]  # not connected
  J87 = female pin header, 2 pins [form="♀ (female)"]  # not connected
  J88 = female pin header, 2 pins [form="♀ (female)"]  # not connected
  J89 = female pin header, 2 pins [form="♀ (female)"]  # not connected
  J90 = female pin header, 2 pins [form="♀ (female)"]  # not connected
  J91 = female pin header, 2 pins [form="♀ (female)"]  # not connected
  J92 = female pin header, 2 pins [form="♀ (female)"]  # not connected
  J93 = female pin header, 2 pins [form="♀ (female)"]  # not connected
  J94 = female pin header, 2 pins [form="♀ (female)"]  # not connected
  J95 = female pin header, 2 pins [form="♀ (female)"]  # not connected
  J96 = female pin header, 2 pins [form="♀ (female)"]  # not connected
  J97 = female pin header, 2 pins [form="♀ (female)"]  # not connected
  J98 = female pin header, 2 pins [form="♀ (female)"]  # not connected
  J99 = female pin header, 2 pins [form="♀ (female)"]  # not connected
  J100 = female pin header, 2 pins [form="♀ (female)"]  # not connected
  J101 = female pin header, 2 pins [form="♀ (female)"]  # not connected
  J102 = female pin header, 2 pins [form="♀ (female)"]  # not connected
  J103 = female pin header, 2 pins [form="♀ (female)"]  # not connected
  J104 = female pin header, 2 pins [form="♀ (female)"]  # not connected
  J105 = female pin header, 2 pins [form="♀ (female)"]  # not connected
  J106 = female pin header, 2 pins [form="♀ (female)"]  # not connected
  J107 = female pin header, 2 pins [form="♀ (female)"]  # not connected
  J108 = female pin header, 2 pins [form="♀ (female)"]  # not connected
  J109 = female pin header, 2 pins [form="♀ (female)"]  # not connected
  J110 = female pin header, 2 pins [form="♀ (female)"]  # not connected
  J111 = female pin header, 2 pins [form="♀ (female)"]  # not connected
  J112 = female pin header, 2 pins [form="♀ (female)"]  # not connected
  J113 = female pin header, 2 pins [form="♀ (female)"]  # not connected
  J114 = female pin header, 2 pins [form="♀ (female)"]  # not connected
  J115 = female pin header, 2 pins [form="♀ (female)"]  # not connected
  J116 = female pin header, 2 pins [form="♀ (female)"]  # not connected
  J117 = female pin header, 2 pins [form="♀ (female)"]  # not connected
  J118 = female pin header, 2 pins [form="♀ (female)"]  # not connected
  J119 = female pin header, 2 pins [form="♀ (female)"]  # not connected
  J120 = female pin header, 2 pins [form="♀ (female)"]  # not connected
  J121 = female pin header, 2 pins [form="♀ (female)"]  # not connected
  J122 = female pin header, 2 pins [form="♀ (female)"]  # not connected
  J123 = female pin header, 2 pins [form="♀ (female)"]  # not connected
  J124 = female pin header, 2 pins [form="♀ (female)"]  # not connected
  J125 = female pin header, 2 pins [form="♀ (female)"]  # not connected
  J126 = female pin header, 2 pins [form="♀ (female)"]  # not connected
  J127 = female pin header, 2 pins [form="♀ (female)"]  # not connected
  J128 = female pin header, 2 pins [form="♀ (female)"]  # not connected
  J129 = female pin header, 2 pins [form="♀ (female)"]  # not connected
  J130 = female pin header, 2 pins [form="♀ (female)"]  # not connected
  J131 = female pin header, 2 pins [form="♀ (female)"]  # not connected
  J132 = female pin header, 2 pins [form="♀ (female)"]  # not connected
  J133 = female pin header, 2 pins [form="♀ (female)"]  # not connected
  J134 = female pin header, 2 pins [form="♀ (female)"]  # not connected
  J135 = female pin header, 2 pins [form="♀ (female)"]  # not connected
  J136 = female pin header, 2 pins [form="♀ (female)"]  # not connected
  J137 = female pin header, 2 pins [form="♀ (female)"]  # not connected
  J138 = female pin header, 2 pins [form="♀ (female)"]  # not connected
  J139 = female pin header, 2 pins [form="♀ (female)"]  # not connected
  J140 = female pin header, 2 pins [form="♀ (female)"]  # not connected
  J141 = female pin header, 2 pins [form="♀ (female)"]  # not connected
  J142 = female pin header, 2 pins [form="♀ (female)"]  # not connected
  J143 = female pin header, 2 pins [form="♀ (female)"]  # not connected
  J144 = female pin header, 2 pins [form="♀ (female)"]  # not connected
  J145 = female pin header, 2 pins [form="♀ (female)"]  # not connected
  J146 = female pin header, 2 pins [form="♀ (female)"]  # not connected
  J147 = female pin header, 2 pins [form="♀ (female)"]  # not connected
  J148 = female pin header, 2 pins [form="♀ (female)"]  # not connected
  J149 = female pin header, 2 pins [form="♀ (female)"]  # not connected
  J150 = female pin header, 2 pins [form="♀ (female)"]  # not connected
  J151 = female pin header, 2 pins [form="♀ (female)"]  # not connected
  J152 = female pin header, 2 pins [form="♀ (female)"]  # not connected
  J153 = female pin header, 2 pins [form="♀ (female)"]  # not connected
  J154 = female pin header, 2 pins [form="♀ (female)"]  # not connected
  J155 = female pin header, 2 pins [form="♀ (female)"]  # not connected
  J156 = female pin header, 2 pins [form="♀ (female)"]  # not connected
  J157 = female pin header, 2 pins [form="♀ (female)"]  # not connected
  J158 = female pin header, 2 pins [form="♀ (female)"]  # not connected
  J159 = female pin header, 2 pins [form="♀ (female)"]  # not connected
  J160 = female pin header, 2 pins [form="♀ (female)"]  # not connected
  U25 = 74HC595 [package="DIP16 [THT]"]
  ICSP = AVR ISP 6 Pin [package=2x3-ns]
  ICSP_U2 = AVR ISP 6 Pin [package=2x3-ns]
  R1 = Resistor [tolerance=±5% resistance=10k package="1206 [SMD]"]
  D1 = smd LED [color="Red (633nm)" package="1206 [SMD]"]
  R2 = Resistor [tolerance=±5% resistance=1k package="0603 [SMD]"]
  R3 = Resistor [tolerance=±5% resistance=1k package="0603 [SMD]"]
  USB_b = USB+SHIELD [package=usb-b-pth]
  Z1 = VARISTOR [package=0603-res]
  Z2 = VARISTOR [package=0603-res]
  C1 = Capacitor [package=0805]
  L1 = Inductors [package=0805]
  C2 = Capacitor [package=0603-cap]
  F1 = Resettable Fuse PTC [package=ptc-1206]
  C3 = Capacitor [package=0603-cap]
  LED1 = smd LED [color="Yellow (585nm)" package="0603 [SMD]"]
  R6 = Resistor [tolerance=±5% resistance=1k package="0603 [SMD]"]
  LED2 = smd LED [color="Yellow (585nm)" package="0603 [SMD]"]
  R7 = Resistor [tolerance=±5% resistance=1k package="0603 [SMD]"]
  U2 = Voltage Regulator LDO [package=sot23-5]
  VIN_GND = female pin header, 2 pins [form="♀ (female)"]
  R8 = Resistor [tolerance=±5% resistance=10k package="1206 [SMD]"]
  R9 = Resistor [tolerance=±5% resistance=10k package="1206 [SMD]"]
  C4 = Capacitor [package=0603-cap]
  R4 = Resistor [tolerance=±5% resistance=220 package="0402 [SMD]"]
  R5 = Resistor [tolerance=±5% resistance=220 package="0402 [SMD]"]
  U3 = LMV358 [package=so08]
  C5 = Capacitor [package=0603-cap]
  U4 = MOSFET-PCHANNEL [package=sot23-3]
  C6 = Capacitor [package=0805]
  RESET = Pushbutton [package="[SMD]"]
  pin_1_pin_2 = female pin header, 2 pins [form="♀ (female)"]
  pin_3_pin_4 = female pin header, 2 pins [form="♀ (female)"]
  RESET-EN = female pin header, 2 pins [form="♀ (female)"]
  C7 = Capacitor [package=0603-cap]
  R10 = Resistor [tolerance=±5% resistance=1k package="0603 [SMD]"]
  XTAL1 = Crystal [frequency="16 Mhz" package=THT]
  R11 = Resistor [tolerance=±5% resistance=1M package="0805 [SMD]"]
  C8 = Capacitor [package=0805]
  C9 = Capacitor [package=0805]
  U5 = LMV358 [package=so08]
  R12 = Resistor [tolerance=±5% resistance=1k package="0603 [SMD]"]
  LED3 = smd LED [color="Yellow (585nm)" package="0603 [SMD]"]
  LED4 = smd LED [color="Green (555nm)" package="0603 [SMD]"]
  R13 = Resistor [tolerance=±5% resistance=1k package="0603 [SMD]"]
  R14 = Resistor [tolerance=±5% resistance=1M package="0805 [SMD]"]
  U6 = Resonator [package=resonator-pth]
  C10 = Capacitor [package=0603-cap]
  C11 = Capacitor [package=0603-cap]
  C12 = Capacitor [package=0603-cap]
  C13 = Capacitor [package=0603-cap]
  R16 = Resistor [tolerance=±5% resistance=10k package="1206 [SMD]"]
  R15 = Resistor [tolerance=±5% resistance=10k package="1206 [SMD]"]
  D2 = smd LED [color="Red (633nm)" package="1206 [SMD]"]
  R17 = Resistor [tolerance=±5% resistance=10k package="1206 [SMD]"]
  C14 = Capacitor [package=0805]
  Register_1 = 74HC595 SMD [package="SO16 [SMD]"]
  U7 = ATmega16U2 [package=QFN-32]
  J183 = double row female pin header, 8 pins [form="♀ (female)"]
  J192 = double row female pin header, 8 pins [form="♀ (female)"]
  BACKUP = 74HC595 SMD [package="SO16 [SMD]"]
  J193 = double row female pin header, 8 pins [form="♀ (female)"]
  Register_2 = 74HC595 SMD [package="SO16 [SMD]"]
  J194 = double row female pin header, 8 pins [form="♀ (female)"]
  Register_3 = 74HC595 SMD [package="SO16 [SMD]"]
  J195 = double row female pin header, 8 pins [form="♀ (female)"]
  J196 = double row female pin header, 8 pins [form="♀ (female)"]
  J197 = double row female pin header, 8 pins [form="♀ (female)"]
  Register_4 = 74HC595 SMD [package="SO16 [SMD]"]
  Register_5 = 74HC595 SMD [package="SO16 [SMD]"]
  Register_6 = 74HC595 SMD [package="SO16 [SMD]"]
  J198 = double row female pin header, 8 pins [form="♀ (female)"]
  J199 = double row female pin header, 8 pins [form="♀ (female)"]
  Register_8 = 74HC595 SMD [package="SO16 [SMD]"]
  Register_7 = 74HC595 SMD [package="SO16 [SMD]"]
  J200 = double row female pin header, 8 pins [form="♀ (female)"]
  J201 = double row female pin header, 8 pins [form="♀ (female)"]
  J202 = double row female pin header, 8 pins [form="♀ (female)"]
  J203 = double row female pin header, 8 pins [form="♀ (female)"]
  J204 = double row female pin header, 8 pins [form="♀ (female)"]
  J205 = double row female pin header, 8 pins [form="♀ (female)"]
  J206 = double row female pin header, 8 pins [form="♀ (female)"]
  J207 = double row female pin header, 8 pins [form="♀ (female)"]
  Register_9 = 74HC595 SMD [package="SO16 [SMD]"]
  Register_10 = 74HC595 SMD [package="SO16 [SMD]"]
  Register_11 = 74HC595 SMD [package="SO16 [SMD]"]
  Register_12 = 74HC595 SMD [package="SO16 [SMD]"]
  Register_13 = 74HC595 SMD [package="SO16 [SMD]"]
  Register_14 = 74HC595 SMD [package="SO16 [SMD]"]
  Register_15 = 74HC595 SMD [package="SO16 [SMD]"]
  Register_16 = 74HC595 SMD [package="SO16 [SMD]"]
  J208 = double row female pin header, 8 pins [form="♀ (female)"]
  J209 = double row female pin header, 8 pins [form="♀ (female)"]
  J210 = double row female pin header, 8 pins [form="♀ (female)"]
  J211 = double row female pin header, 8 pins [form="♀ (female)"]
  J212 = double row female pin header, 8 pins [form="♀ (female)"]
  J213 = double row female pin header, 8 pins [form="♀ (female)"]
  J214 = double row female pin header, 8 pins [form="♀ (female)"]
  J215 = double row female pin header, 8 pins [form="♀ (female)"]
  J216 = double row female pin header, 8 pins [form="♀ (female)"]
  J217 = double row female pin header, 8 pins [form="♀ (female)"]
  J218 = double row female pin header, 8 pins [form="♀ (female)"]
  J219 = double row female pin header, 8 pins [form="♀ (female)"]
  J220 = double row female pin header, 8 pins [form="♀ (female)"]
  J221 = double row female pin header, 8 pins [form="♀ (female)"]
  J222 = double row female pin header, 8 pins [form="♀ (female)"]
  J223 = double row female pin header, 8 pins [form="♀ (female)"]
  Register_17 = 74HC595 SMD [package="SO16 [SMD]"]
  Register_18 = 74HC595 SMD [package="SO16 [SMD]"]
  Register_19 = 74HC595 SMD [package="SO16 [SMD]"]
  Register_20 = 74HC595 SMD [package="SO16 [SMD]"]
  Register_21 = 74HC595 SMD [package="SO16 [SMD]"]
  Register_22 = 74HC595 SMD [package="SO16 [SMD]"]
  Register_23 = 74HC595 SMD [package="SO16 [SMD]"]
  Register_24 = 74HC595 SMD [package="SO16 [SMD]"]
  Register_25 = 74HC595 SMD [package="SO16 [SMD]"]
  Register_26 = 74HC595 SMD [package="SO16 [SMD]"]
  Register_27 = 74HC595 SMD [package="SO16 [SMD]"]
  Register_28 = 74HC595 SMD [package="SO16 [SMD]"]
  Register_29 = 74HC595 SMD [package="SO16 [SMD]"]
  Register_30 = 74HC595 SMD [package="SO16 [SMD]"]
  Register_31 = 74HC595 SMD [package="SO16 [SMD]"]
  Register_32 = 74HC595 SMD [package="SO16 [SMD]"]
  J224 = double row female pin header, 8 pins [form="♀ (female)"]
  J225 = double row female pin header, 8 pins [form="♀ (female)"]
  J226 = double row female pin header, 8 pins [form="♀ (female)"]
  J227 = double row female pin header, 8 pins [form="♀ (female)"]
  J228 = double row female pin header, 8 pins [form="♀ (female)"]
  J229 = double row female pin header, 8 pins [form="♀ (female)"]
  J230 = double row female pin header, 8 pins [form="♀ (female)"]
  J231 = double row female pin header, 8 pins [form="♀ (female)"]
  Register_33 = 74HC595 SMD [package="SO16 [SMD]"]
  Register_34 = 74HC595 SMD [package="SO16 [SMD]"]
  Register_35 = 74HC595 SMD [package="SO16 [SMD]"]
  Register_36 = 74HC595 SMD [package="SO16 [SMD]"]
  Register_37 = 74HC595 SMD [package="SO16 [SMD]"]
  Register_38 = 74HC595 SMD [package="SO16 [SMD]"]
  Register_39 = 74HC595 SMD [package="SO16 [SMD]"]
  Register_40 = 74HC595 SMD [package="SO16 [SMD]"]
  J232 = double row female pin header, 8 pins [form="♀ (female)"]
  J233 = double row female pin header, 8 pins [form="♀ (female)"]
  J234 = double row female pin header, 8 pins [form="♀ (female)"]
  J235 = double row female pin header, 8 pins [form="♀ (female)"]
  J236 = double row female pin header, 8 pins [form="♀ (female)"]
  J237 = double row female pin header, 8 pins [form="♀ (female)"]
  J238 = double row female pin header, 8 pins [form="♀ (female)"]
  J239 = double row female pin header, 8 pins [form="♀ (female)"]
  Register_41 = 74HC595 SMD [package="SO16 [SMD]"]
  Register_42 = 74HC595 SMD [package="SO16 [SMD]"]
  Register_43 = 74HC595 SMD [package="SO16 [SMD]"]
  Register_44 = 74HC595 SMD [package="SO16 [SMD]"]
  Register_45 = 74HC595 SMD [package="SO16 [SMD]"]
  Register_46 = 74HC595 SMD [package="SO16 [SMD]"]
  Register_47 = 74HC595 SMD [package="SO16 [SMD]"]
  Register_48 = 74HC595 SMD [package="SO16 [SMD]"]
  J240 = double row female pin header, 8 pins [form="♀ (female)"]
  J241 = double row female pin header, 8 pins [form="♀ (female)"]
  J242 = double row female pin header, 8 pins [form="♀ (female)"]
  J243 = double row female pin header, 8 pins [form="♀ (female)"]
  J244 = double row female pin header, 8 pins [form="♀ (female)"]
  J245 = double row female pin header, 8 pins [form="♀ (female)"]
  J246 = double row female pin header, 8 pins [form="♀ (female)"]
  J247 = double row female pin header, 8 pins [form="♀ (female)"]
  J248 = double row female pin header, 8 pins [form="♀ (female)"]
  J249 = double row female pin header, 8 pins [form="♀ (female)"]
  J250 = double row female pin header, 8 pins [form="♀ (female)"]
  J251 = double row female pin header, 8 pins [form="♀ (female)"]
  J252 = double row female pin header, 8 pins [form="♀ (female)"]
  J253 = double row female pin header, 8 pins [form="♀ (female)"]
  J254 = double row female pin header, 8 pins [form="♀ (female)"]
  J255 = double row female pin header, 8 pins [form="♀ (female)"]
  Register_49 = 74HC595 SMD [package="SO16 [SMD]"]
  Register_50 = 74HC595 SMD [package="SO16 [SMD]"]
  Register_51 = 74HC595 SMD [package="SO16 [SMD]"]
  Register_52 = 74HC595 SMD [package="SO16 [SMD]"]
  Register_53 = 74HC595 SMD [package="SO16 [SMD]"]
  Register_54 = 74HC595 SMD [package="SO16 [SMD]"]
  Register_55 = 74HC595 SMD [package="SO16 [SMD]"]
  Register_56 = 74HC595 SMD [package="SO16 [SMD]"]
  Register_57 = 74HC595 SMD [package="SO16 [SMD]"]
  Register_58 = 74HC595 SMD [package="SO16 [SMD]"]
  Register_59 = 74HC595 SMD [package="SO16 [SMD]"]
  Register_60 = 74HC595 SMD [package="SO16 [SMD]"]
  Register_61 = 74HC595 SMD [package="SO16 [SMD]"]
  Register_62 = 74HC595 SMD [package="SO16 [SMD]"]
  Register_63 = 74HC595 SMD [package="SO16 [SMD]"]
  Register_64 = 74HC595 SMD [package="SO16 [SMD]"]

nets:
  N1: Arduino_Mega_2560_(Rev_3).D21/SCL, U15.DS
  N2: Arduino_Mega_2560_(Rev_3).D20/SDA, U14.SH_CP
  N3: Arduino_Mega_2560_(Rev_3).D19/RX1, U14.ST_CP
  N4: Arduino_Mega_2560_(Rev_3).D18/TX1, U14.DS
  N5: Arduino_Mega_2560_(Rev_3).D17_PWM/RX2, U13.SH_CP
  N6: Arduino_Mega_2560_(Rev_3).D16_PWM/TX2, U13.ST_CP
  N7: Arduino_Mega_2560_(Rev_3).D15/RX3, U13.DS
  N8: Arduino_Mega_2560_(Rev_3).D14/TX3, U12.SH_CP
  N9: Arduino_Mega_2560_(Rev_3).D13_PWM, U12.ST_CP
  N10: Arduino_Mega_2560_(Rev_3).D12_PWM, U12.DS
  N11: Arduino_Mega_2560_(Rev_3).D11_PWM, U11.SH_CP
  N12: Arduino_Mega_2560_(Rev_3).D10_PWM, U11.ST_CP
  N13: Arduino_Mega_2560_(Rev_3).D9_PWM, U11.DS
  N14: Arduino_Mega_2560_(Rev_3).D8_PWM, U10.SH_CP
  VCC: Arduino_Mega_2560_(Rev_3).5V, U8.MR, U8.VCC, U9.MR, U9.VCC, U10.MR, U10.VCC, U11.MR, U11.VCC, U12.MR, U12.VCC, U13.MR, U13.VCC, U14.MR, U14.VCC, U15.MR, U15.VCC, U16.MR, U16.VCC, U17.MR, U17.VCC, U18.MR, U18.VCC, U19.MR, U19.VCC, U20.MR, U20.VCC, U21.MR, U21.VCC, U22.MR, U22.VCC, U23.MR, U23.VCC, U24.MR, U24.VCC, U25.MR, U25.VCC
  GND: Arduino_Mega_2560_(Rev_3).GND, U8.GND, U8.OE, U9.GND, U9.OE, U10.GND, U10.OE, U11.GND, U11.OE, U12.GND, U12.OE, U13.GND, U13.OE, U14.GND, U14.OE, U15.GND, U15.OE, U16.GND, U16.OE, U17.GND, U17.OE, U18.GND, U18.OE, U19.GND, U19.OE, U20.GND, U20.OE, U21.GND, U21.OE, U22.GND, U22.OE, U23.GND, U23.OE, U24.GND, U24.OE, U25.GND, U25.OE
  N15: Arduino_Mega_2560_(Rev_3).D0_RX0, U25.DS
  N16: Arduino_Mega_2560_(Rev_3).D1_TX0, U25.ST_CP
  N17: Arduino_Mega_2560_(Rev_3).D2_PWM, U25.SH_CP
  N18: Arduino_Mega_2560_(Rev_3).D3_PWM, U9.DS
  N19: Arduino_Mega_2560_(Rev_3).D4_PWM, U9.ST_CP
  N20: Arduino_Mega_2560_(Rev_3).D5_PWM, U9.SH_CP
  N21: Arduino_Mega_2560_(Rev_3).D6_PWM, U10.DS
  N22: Arduino_Mega_2560_(Rev_3).D7_PWM, U10.ST_CP
  N23: Arduino_Mega_2560_(Rev_3).D22, U15.ST_CP
  N24: Arduino_Mega_2560_(Rev_3).D23, U15.SH_CP
  N25: Arduino_Mega_2560_(Rev_3).D24, U16.DS
  N26: Arduino_Mega_2560_(Rev_3).D25, U16.ST_CP
  N27: Arduino_Mega_2560_(Rev_3).D26, U16.SH_CP
  N28: Arduino_Mega_2560_(Rev_3).D27, U17.DS
  N29: Arduino_Mega_2560_(Rev_3).D28, U17.ST_CP
  N30: Arduino_Mega_2560_(Rev_3).D29, U17.SH_CP
  N31: Arduino_Mega_2560_(Rev_3).D30, U18.DS
  N32: Arduino_Mega_2560_(Rev_3).D31, U18.ST_CP
  N33: Arduino_Mega_2560_(Rev_3).D32, U18.SH_CP
  N34: Arduino_Mega_2560_(Rev_3).D33, U19.DS
  N35: Arduino_Mega_2560_(Rev_3).D34, U19.ST_CP
  N36: Arduino_Mega_2560_(Rev_3).D35, U19.SH_CP
  N37: Arduino_Mega_2560_(Rev_3).D36, U20.DS
  N38: Arduino_Mega_2560_(Rev_3).D37, U20.ST_CP
  N39: Arduino_Mega_2560_(Rev_3).D38, U20.SH_CP
  N40: Arduino_Mega_2560_(Rev_3).D39, U21.DS
  N41: Arduino_Mega_2560_(Rev_3).D40, U21.ST_CP
  N42: Arduino_Mega_2560_(Rev_3).D41, U21.SH_CP
  N43: Arduino_Mega_2560_(Rev_3).D42, U22.DS
  N44: Arduino_Mega_2560_(Rev_3).D43, U22.ST_CP
  N45: Arduino_Mega_2560_(Rev_3).D44, U22.SH_CP
  N46: Arduino_Mega_2560_(Rev_3).D45, U23.DS
  N47: Arduino_Mega_2560_(Rev_3).D46, U23.ST_CP
  N48: Arduino_Mega_2560_(Rev_3).D47, U23.SH_CP
  N49: Arduino_Mega_2560_(Rev_3).D48, U24.DS
  N50: Arduino_Mega_2560_(Rev_3).D49, U24.ST_CP
  N51: Arduino_Mega_2560_(Rev_3).D50, U24.SH_CP
  N52: Arduino_Mega_2560_(Rev_3).D51, U8.DS
  N53: Arduino_Mega_2560_(Rev_3).D52, U8.ST_CP
  N54: Arduino_Mega_2560_(Rev_3).D53, U8.SH_CP
  N55: ATmega_2560_16au.(RXD0_PCIN8)PE0, R3.Pin_0
  N56: ATmega_2560_16au.(TXD0)PE1, R2.Pin_0
  VCC_2: ATmega_2560_16au.VCC, ATmega_2560_16au.VCC1, ATmega_2560_16au.VCC2, ATmega_2560_16au.VCC3, ATmega_2560_16au.AVCC, ICSP.2, ICSP_U2.2, R1.Pin_0, D1.cathode, C2.2, R6.Pin_1, R7.Pin_1, U2.IN, U2.EN, U3.G$1_+V, C5.1, U4.S, R13.Pin_1, C11.1, C12.1, C13.1, R16.Pin_0, R15.Pin_0, D2.cathode, R17.Pin_0, U7.VCC, U7.AVCC
  GND_2: ATmega_2560_16au.GND, ATmega_2560_16au.GND1, ATmega_2560_16au.GND2, ATmega_2560_16au.GND3, ATmega_2560_16au.AGND, ICSP.6, ICSP_U2.6, C2.1, C3.1, U2.GND, VIN_GND.pin1, R9.Pin_1, C4.2, U3.G$1_GND, C5.2, C6.1, RESET.Pin_3, RESET.Pin_4, R10.Pin_0, C8.1, C9.1, LED3.cathode, LED4.cathode, U6.2, C10.2, C11.2, C12.2, C13.2, C14.2, U7.GND, U7.Pad_GND
  N57: ATmega_2560_16au.(SCK_PCINT1)PB1, ICSP.3
  N58: ATmega_2560_16au.(MOSI_PCINT2)PB2, ICSP.4
  N59: ATmega_2560_16au.(MISO_PCINT3)PB3, ICSP.1
  N60: ATmega_2560_16au.(OC0A_OC1C_PCINT7)PB7, U5.G$1_+IN1
  N61: ATmega_2560_16au.RESET, ICSP.5, RESET.Pin_2, D2.anode, R17.Pin_1, C14.1
  N62: ATmega_2560_16au.XTAL2, R14.Pin_0, U6.1
  N63: ATmega_2560_16au.XTAL1, R14.Pin_1, U6.3
  N64: ATmega_2560_16au.(SCL_INT0)PD0, R15.Pin_1
  N65: ATmega_2560_16au.(SDA_INT1)PD1, R16.Pin_1
  N66: ATmega_2560_16au.AREF, C10.1
  N67: ICSP_U2.1, U7.PB3
  N68: ICSP_U2.3, U7.PB1
  N69: ICSP_U2.4, U7.PB2
  N70: ICSP_U2.5, R1.Pin_1, D1.anode, RESET-EN.pin1, RESET-EN.pin2, C7.2, U7.Reset
  N71: R2.Pin_1, U7.PD2
  N72: R3.Pin_1, U7.PD3
  N73: USB_b.P$1, USB_b.P$2, Z1.2, Z2.2, L1.2
  N74: USB_b.D+, Z2.1, R4.Pin_1
  N75: USB_b.D-, Z1.1, R5.Pin_1
  N76: USB_b.GND, C1.2, L1.1, U7.UGND
  N77: USB_b.VBUS, F1.2
  N78: C1.1, U7.UCAP
  N79: F1.1, C3.2, U4.D, U7.UVCC
  N80: LED1.cathode, U7.PD5
  N81: LED1.anode, R6.Pin_0
  N82: LED2.cathode, U7.PD4
  N83: LED2.anode, R7.Pin_0
  N84: U2.OUT, U3.G$2_-IN2, C6.2
  N85: VIN_GND.pin2, R8.Pin_0
  N86: R8.Pin_1, R9.Pin_0, C4.1, U3.G$2_+IN2
  N87: R4.Pin_0, U7.D+
  N88: R5.Pin_0, U7.D-
  N89: U3.G$2_OUT2, U4.G
  N90: pin_1_pin_2.pin1, U7.PB6
  N91: pin_1_pin_2.pin2, U7.PB4
  N92: pin_3_pin_4.pin1, U7.PB7
  N93: pin_3_pin_4.pin2, U7.PB5
  N94: C7.1, R10.Pin_1, U7.PD7
  N95: XTAL1.pin_0, R11.Pin_0, C8.2, U7.XTAL1
  N96: XTAL1.pin_1, R11.Pin_1, C9.2, U7.XTAL2
  N97: U5.G$1_OUT1, U5.G$1_-IN1, R12.Pin_1
  N98: R12.Pin_0, LED3.anode
  N99: LED4.anode, R13.Pin_0
  N100: Register_1.Q1, J183.pin3
  N101: Register_1.Q2, J183.pin2
  N102: Register_1.Q3, J183.pin1
  N103: Register_1.Q4, J183.pin5
  N104: Register_1.Q5, J183.pin6
  N105: Register_1.Q6, J183.pin7
  N106: Register_1.Q7, J183.pin8
  GND_3: Register_1.GND, Register_1.OE, Register_2.GND, Register_2.OE, Register_3.GND, Register_3.OE, Register_4.GND, Register_4.OE, Register_5.GND, Register_5.OE, Register_6.GND, Register_6.OE, Register_8.GND, Register_8.OE, Register_7.GND, Register_7.OE, Register_9.GND, Register_9.OE, Register_10.GND, Register_10.OE, Register_11.GND, Register_11.OE, Register_12.GND, Register_12.OE, Register_13.GND, Register_13.OE, Register_14.GND, Register_14.OE, Register_15.GND, Register_15.OE, Register_16.GND, Register_16.OE, Register_17.GND, Register_17.OE, Register_18.GND, Register_18.OE, Register_19.GND, Register_19.OE, Register_20.GND, Register_20.OE, Register_21.GND, Register_21.OE, Register_22.GND, Register_22.OE, Register_23.GND, Register_23.OE, Register_24.GND, Register_24.OE, Register_25.GND, Register_25.OE, Register_26.GND, Register_26.OE, Register_27.GND, Register_27.OE, Register_28.GND, Register_28.OE, Register_29.GND, Register_29.OE, Register_30.GND, Register_30.OE, Register_31.GND, Register_31.OE, Register_32.GND, Register_32.OE, Register_33.GND, Register_33.OE, Register_34.GND, Register_34.OE, Register_35.GND, Register_35.OE, Register_36.GND, Register_36.OE, Register_37.GND, Register_37.OE, Register_38.GND, Register_38.OE, Register_39.GND, Register_39.OE, Register_40.GND, Register_40.OE, Register_41.GND, Register_41.OE, Register_42.GND, Register_42.OE, Register_43.GND, Register_43.OE, Register_44.GND, Register_44.OE, Register_45.GND, Register_45.OE, Register_46.GND, Register_46.OE, Register_47.GND, Register_47.OE, Register_48.GND, Register_48.OE, Register_49.GND, Register_49.OE, Register_50.GND, Register_50.OE, Register_51.GND, Register_51.OE, Register_52.GND, Register_52.OE, Register_53.GND, Register_53.OE, Register_54.GND, Register_54.OE, Register_55.GND, Register_55.OE, Register_56.GND, Register_56.OE, Register_57.GND, Register_57.OE, Register_58.GND, Register_58.OE, Register_59.GND, Register_59.OE, Register_60.GND, Register_60.OE, Register_61.GND, Register_61.OE, Register_62.GND, Register_62.OE, Register_63.GND, Register_63.OE, Register_64.GND, Register_64.OE
  N107: Register_1.Q7', Register_2.DS
  N108: Register_1.MR, Register_1.VCC
  N109: Register_1.SH_CP, Register_2.SH_CP, Register_3.SH_CP, Register_4.SH_CP, Register_5.SH_CP, Register_6.SH_CP, Register_8.SH_CP, Register_7.SH_CP
  N110: Register_1.ST_CP, Register_2.ST_CP, Register_3.ST_CP, Register_4.ST_CP, Register_5.ST_CP, Register_6.ST_CP, Register_8.ST_CP, Register_7.ST_CP
  N111: Register_1.Q0, J183.pin4
  N112: J192.pin1, BACKUP.Q6
  N113: J192.pin2, BACKUP.Q4
  N114: J192.pin3, BACKUP.Q2
  N115: J192.pin4, BACKUP.Q0
  N116: J192.pin5, BACKUP.Q1
  N117: J192.pin6, BACKUP.Q3
  N118: J192.pin7, BACKUP.Q5
  N119: J192.pin8, BACKUP.Q7
  N120: BACKUP.GND, BACKUP.OE
  N121: BACKUP.MR, BACKUP.VCC
  N122: J193.pin1, Register_2.Q3
  N123: J193.pin2, Register_2.Q2
  N124: J193.pin3, Register_2.Q1
  N125: J193.pin4, Register_2.Q0
  N126: J193.pin5, Register_2.Q4
  N127: J193.pin6, Register_2.Q5
  N128: J193.pin7, Register_2.Q6
  N129: J193.pin8, Register_2.Q7
  N130: Register_2.Q7', Register_3.DS
  N131: Register_2.MR, Register_2.VCC
  N132: J194.pin1, Register_3.Q3
  N133: J194.pin2, Register_3.Q2
  N134: J194.pin3, Register_3.Q1
  N135: J194.pin4, Register_3.Q0
  N136: J194.pin5, Register_3.Q4
  N137: J194.pin6, Register_3.Q5
  N138: J194.pin7, Register_3.Q6
  N139: J194.pin8, Register_3.Q7
  N140: Register_3.Q7', Register_4.DS
  N141: Register_3.MR, Register_3.VCC
  N142: J195.pin1, Register_4.Q3
  N143: J195.pin2, Register_4.Q2
  N144: J195.pin3, Register_4.Q1
  N145: J195.pin4, Register_4.Q0
  N146: J195.pin5, Register_4.Q4
  N147: J195.pin6, Register_4.Q5
  N148: J195.pin7, Register_4.Q6
  N149: J195.pin8, Register_4.Q7
  N150: J196.pin1, Register_5.Q3
  N151: J196.pin2, Register_5.Q2
  N152: J196.pin3, Register_5.Q1
  N153: J196.pin4, Register_5.Q0
  N154: J196.pin5, Register_5.Q4
  N155: J196.pin6, Register_5.Q5
  N156: J196.pin7, Register_5.Q6
  N157: J196.pin8, Register_5.Q7
  N158: J197.pin1, Register_6.Q3
  N159: J197.pin2, Register_6.Q2
  N160: J197.pin3, Register_6.Q1
  N161: J197.pin4, Register_6.Q0
  N162: J197.pin5, Register_6.Q4
  N163: J197.pin6, Register_6.Q5
  N164: J197.pin7, Register_6.Q6
  N165: J197.pin8, Register_6.Q7
  N166: Register_4.Q7', Register_5.DS
  N167: Register_4.MR, Register_4.VCC
  N168: Register_5.Q7', Register_6.DS
  N169: Register_5.MR, Register_5.VCC
  N170: Register_6.Q7', Register_7.DS
  N171: Register_6.MR, Register_6.VCC
  N172: J198.pin1, Register_8.Q3
  N173: J198.pin2, Register_8.Q2
  N174: J198.pin3, Register_8.Q1
  N175: J198.pin4, Register_8.Q0
  N176: J198.pin5, Register_8.Q4
  N177: J198.pin6, Register_8.Q5
  N178: J198.pin7, Register_8.Q6
  N179: J198.pin8, Register_8.Q7
  N180: J199.pin1, Register_7.Q3
  N181: J199.pin2, Register_7.Q2
  N182: J199.pin3, Register_7.Q1
  N183: J199.pin4, Register_7.Q0
  N184: J199.pin5, Register_7.Q4
  N185: J199.pin6, Register_7.Q5
  N186: J199.pin7, Register_7.Q6
  N187: J199.pin8, Register_7.Q7
  N188: Register_8.MR, Register_8.VCC
  N189: Register_8.DS, Register_7.Q7'
  N190: Register_7.MR, Register_7.VCC
  N191: J200.pin1, Register_9.Q3
  N192: J200.pin2, Register_9.Q2
  N193: J200.pin3, Register_9.Q1
  N194: J200.pin4, Register_9.Q0
  N195: J200.pin5, Register_9.Q4
  N196: J200.pin6, Register_9.Q5
  N197: J200.pin7, Register_9.Q6
  N198: J200.pin8, Register_9.Q7
  N199: J201.pin1, Register_10.Q3
  N200: J201.pin2, Register_10.Q2
  N201: J201.pin3, Register_10.Q1
  N202: J201.pin4, Register_10.Q0
  N203: J201.pin5, Register_10.Q4
  N204: J201.pin6, Register_10.Q5
  N205: J201.pin7, Register_10.Q6
  N206: J201.pin8, Register_10.Q7
  N207: J202.pin1, Register_11.Q3
  N208: J202.pin2, Register_11.Q2
  N209: J202.pin3, Register_11.Q1
  N210: J202.pin4, Register_11.Q0
  N211: J202.pin5, Register_11.Q4
  N212: J202.pin6, Register_11.Q5
  N213: J202.pin7, Register_11.Q6
  N214: J202.pin8, Register_11.Q7
  N215: J203.pin1, Register_12.Q3
  N216: J203.pin2, Register_12.Q2
  N217: J203.pin3, Register_12.Q1
  N218: J203.pin4, Register_12.Q0
  N219: J203.pin5, Register_12.Q4
  N220: J203.pin6, Register_12.Q5
  N221: J203.pin7, Register_12.Q6
  N222: J203.pin8, Register_12.Q7
  N223: J204.pin1, Register_13.Q3
  N224: J204.pin2, Register_13.Q2
  N225: J204.pin3, Register_13.Q1
  N226: J204.pin4, Register_13.Q0
  N227: J204.pin5, Register_13.Q4
  N228: J204.pin6, Register_13.Q5
  N229: J204.pin7, Register_13.Q6
  N230: J204.pin8, Register_13.Q7
  N231: J205.pin1, Register_14.Q3
  N232: J205.pin2, Register_14.Q2
  N233: J205.pin3, Register_14.Q1
  N234: J205.pin4, Register_14.Q0
  N235: J205.pin5, Register_14.Q4
  N236: J205.pin6, Register_14.Q5
  N237: J205.pin7, Register_14.Q6
  N238: J205.pin8, Register_14.Q7
  N239: J206.pin1, Register_15.Q3
  N240: J206.pin2, Register_15.Q2
  N241: J206.pin3, Register_15.Q1
  N242: J206.pin4, Register_15.Q0
  N243: J206.pin5, Register_15.Q4
  N244: J206.pin6, Register_15.Q5
  N245: J206.pin7, Register_15.Q6
  N246: J206.pin8, Register_15.Q7
  N247: J207.pin1, Register_16.Q3
  N248: J207.pin2, Register_16.Q2
  N249: J207.pin3, Register_16.Q1
  N250: J207.pin4, Register_16.Q0
  N251: J207.pin5, Register_16.Q4
  N252: J207.pin6, Register_16.Q5
  N253: J207.pin7, Register_16.Q6
  N254: J207.pin8, Register_16.Q7
  N255: Register_9.Q7', Register_12.DS
  N256: Register_9.MR, Register_9.VCC
  N257: Register_9.SH_CP, Register_10.SH_CP, Register_11.SH_CP, Register_12.SH_CP, Register_13.SH_CP, Register_14.SH_CP, Register_15.SH_CP, Register_16.SH_CP
  N258: Register_9.ST_CP, Register_10.ST_CP, Register_11.ST_CP, Register_12.ST_CP, Register_13.ST_CP, Register_14.ST_CP, Register_15.ST_CP, Register_16.ST_CP
  N259: Register_9.DS, Register_11.Q7'
  N260: Register_10.MR, Register_10.VCC
  N261: Register_10.DS, Register_12.Q7'
  N262: Register_11.MR, Register_11.VCC
  N263: Register_11.DS, Register_13.Q7'
  N264: Register_12.MR, Register_12.VCC
  N265: Register_13.MR, Register_13.VCC
  N266: Register_13.DS, Register_14.Q7'
  N267: Register_14.MR, Register_14.VCC
  N268: Register_14.DS, Register_15.Q7'
  N269: Register_15.MR, Register_15.VCC
  N270: Register_15.DS, Register_16.Q7'
  N271: Register_16.MR, Register_16.VCC
  N272: J208.pin1, Register_17.Q3
  N273: J208.pin2, Register_17.Q2
  N274: J208.pin3, Register_17.Q1
  N275: J208.pin4, Register_17.Q0
  N276: J208.pin5, Register_17.Q4
  N277: J208.pin6, Register_17.Q5
  N278: J208.pin7, Register_17.Q6
  N279: J208.pin8, Register_17.Q7
  N280: J209.pin1, Register_20.Q3
  N281: J209.pin2, Register_20.Q2
  N282: J209.pin3, Register_20.Q1
  N283: J209.pin4, Register_20.Q0
  N284: J209.pin5, Register_20.Q4
  N285: J209.pin6, Register_20.Q5
  N286: J209.pin7, Register_20.Q6
  N287: J209.pin8, Register_20.Q7
  N288: J210.pin1, Register_18.Q3
  N289: J210.pin2, Register_18.Q2
  N290: J210.pin3, Register_18.Q1
  N291: J210.pin4, Register_18.Q0
  N292: J210.pin5, Register_18.Q4
  N293: J210.pin6, Register_18.Q5
  N294: J210.pin7, Register_18.Q6
  N295: J210.pin8, Register_18.Q7
  N296: J211.pin1, Register_19.Q3
  N297: J211.pin2, Register_19.Q2
  N298: J211.pin3, Register_19.Q1
  N299: J211.pin4, Register_19.Q0
  N300: J211.pin5, Register_19.Q4
  N301: J211.pin6, Register_19.Q5
  N302: J211.pin7, Register_19.Q6
  N303: J211.pin8, Register_19.Q7
  N304: J212.pin1, Register_21.Q3
  N305: J212.pin2, Register_21.Q2
  N306: J212.pin3, Register_21.Q1
  N307: J212.pin4, Register_21.Q0
  N308: J212.pin5, Register_21.Q4
  N309: J212.pin6, Register_21.Q5
  N310: J212.pin7, Register_21.Q6
  N311: J212.pin8, Register_21.Q7
  N312: J213.pin1, Register_22.Q3
  N313: J213.pin2, Register_22.Q2
  N314: J213.pin3, Register_22.Q1
  N315: J213.pin4, Register_22.Q0
  N316: J213.pin5, Register_22.Q4
  N317: J213.pin6, Register_22.Q5
  N318: J213.pin7, Register_22.Q6
  N319: J213.pin8, Register_22.Q7
  N320: J214.pin1, Register_23.Q3
  N321: J214.pin2, Register_23.Q2
  N322: J214.pin3, Register_23.Q1
  N323: J214.pin4, Register_23.Q0
  N324: J214.pin5, Register_23.Q4
  N325: J214.pin6, Register_23.Q5
  N326: J214.pin7, Register_23.Q6
  N327: J214.pin8, Register_23.Q7
  N328: J215.pin1, Register_24.Q3
  N329: J215.pin2, Register_24.Q2
  N330: J215.pin3, Register_24.Q1
  N331: J215.pin4, Register_24.Q0
  N332: J215.pin5, Register_24.Q4
  N333: J215.pin6, Register_24.Q5
  N334: J215.pin7, Register_24.Q6
  N335: J215.pin8, Register_24.Q7
  N336: J216.pin1, Register_25.Q3
  N337: J216.pin2, Register_25.Q2
  N338: J216.pin3, Register_25.Q1
  N339: J216.pin4, Register_25.Q0
  N340: J216.pin5, Register_25.Q4
  N341: J216.pin6, Register_25.Q5
  N342: J216.pin7, Register_25.Q6
  N343: J216.pin8, Register_25.Q7
  N344: J217.pin1, Register_26.Q3
  N345: J217.pin2, Register_26.Q2
  N346: J217.pin3, Register_26.Q1
  N347: J217.pin4, Register_26.Q0
  N348: J217.pin5, Register_26.Q4
  N349: J217.pin6, Register_26.Q5
  N350: J217.pin7, Register_26.Q6
  N351: J217.pin8, Register_26.Q7
  N352: J218.pin1, Register_27.Q3
  N353: J218.pin2, Register_27.Q2
  N354: J218.pin3, Register_27.Q1
  N355: J218.pin4, Register_27.Q0
  N356: J218.pin5, Register_27.Q4
  N357: J218.pin6, Register_27.Q5
  N358: J218.pin7, Register_27.Q6
  N359: J218.pin8, Register_27.Q7
  N360: J219.pin1, Register_28.Q3
  N361: J219.pin2, Register_28.Q2
  N362: J219.pin3, Register_28.Q1
  N363: J219.pin4, Register_28.Q0
  N364: J219.pin5, Register_28.Q4
  N365: J219.pin6, Register_28.Q5
  N366: J219.pin7, Register_28.Q6
  N367: J219.pin8, Register_28.Q7
  N368: J220.pin1, Register_29.Q3
  N369: J220.pin2, Register_29.Q2
  N370: J220.pin3, Register_29.Q1
  N371: J220.pin4, Register_29.Q0
  N372: J220.pin5, Register_29.Q4
  N373: J220.pin6, Register_29.Q5
  N374: J220.pin7, Register_29.Q6
  N375: J220.pin8, Register_29.Q7
  N376: J221.pin1, Register_30.Q3
  N377: J221.pin2, Register_30.Q2
  N378: J221.pin3, Register_30.Q1
  N379: J221.pin4, Register_30.Q0
  N380: J221.pin5, Register_30.Q4
  N381: J221.pin6, Register_30.Q5
  N382: J221.pin7, Register_30.Q6
  N383: J221.pin8, Register_30.Q7
  N384: J222.pin1, Register_31.Q3
  N385: J222.pin2, Register_31.Q2
  N386: J222.pin3, Register_31.Q1
  N387: J222.pin4, Register_31.Q0
  N388: J222.pin5, Register_31.Q4
  N389: J222.pin6, Register_31.Q5
  N390: J222.pin7, Register_31.Q6
  N391: J222.pin8, Register_31.Q7
  N392: J223.pin1, Register_32.Q3
  N393: J223.pin2, Register_32.Q2
  N394: J223.pin3, Register_32.Q1
  N395: J223.pin4, Register_32.Q0
  N396: J223.pin5, Register_32.Q4
  N397: J223.pin6, Register_32.Q5
  N398: J223.pin7, Register_32.Q6
  N399: J223.pin8, Register_32.Q7
  N400: Register_17.Q7', Register_24.DS
  N401: Register_17.MR, Register_17.VCC
  N402: Register_17.SH_CP, Register_19.SH_CP, Register_21.SH_CP, Register_24.SH_CP, Register_25.SH_CP, Register_27.SH_CP, Register_29.SH_CP, Register_31.SH_CP
  N403: Register_17.ST_CP, Register_19.ST_CP, Register_21.ST_CP, Register_24.ST_CP, Register_25.ST_CP, Register_27.ST_CP, Register_29.ST_CP, Register_31.ST_CP
  N404: Register_17.DS, Register_21.Q7'
  N405: Register_18.Q7', Register_23.DS
  N406: Register_18.MR, Register_18.VCC
  N407: Register_18.SH_CP, Register_20.SH_CP, Register_22.SH_CP, Register_23.SH_CP, Register_26.SH_CP, Register_28.SH_CP, Register_30.SH_CP, Register_32.SH_CP
  N408: Register_18.ST_CP, Register_20.ST_CP, Register_22.ST_CP, Register_23.ST_CP, Register_26.ST_CP, Register_28.ST_CP, Register_30.ST_CP, Register_32.ST_CP
  N409: Register_18.DS, Register_22.Q7'
  N410: Register_19.MR, Register_19.VCC
  N411: Register_19.DS, Register_24.Q7'
  N412: Register_20.MR, Register_20.VCC
  N413: Register_20.DS, Register_23.Q7'
  N414: Register_21.MR, Register_21.VCC
  N415: Register_21.DS, Register_25.Q7'
  N416: Register_22.MR, Register_22.VCC
  N417: Register_22.DS, Register_26.Q7'
  N418: Register_23.MR, Register_23.VCC
  N419: Register_24.MR, Register_24.VCC
  N420: Register_25.MR, Register_25.VCC
  N421: Register_25.DS, Register_27.Q7'
  N422: Register_26.MR, Register_26.VCC
  N423: Register_26.DS, Register_28.Q7'
  N424: Register_27.MR, Register_27.VCC
  N425: Register_27.DS, Register_29.Q7'
  N426: Register_28.MR, Register_28.VCC
  N427: Register_28.DS, Register_30.Q7'
  N428: Register_29.MR, Register_29.VCC
  N429: Register_29.DS, Register_31.Q7'
  N430: Register_30.MR, Register_30.VCC
  N431: Register_30.DS, Register_32.Q7'
  N432: Register_31.MR, Register_31.VCC
  N433: Register_32.MR, Register_32.VCC
  N434: J224.pin1, Register_34.Q3
  N435: J224.pin2, Register_34.Q2
  N436: J224.pin3, Register_34.Q1
  N437: J224.pin4, Register_34.Q0
  N438: J224.pin5, Register_34.Q4
  N439: J224.pin6, Register_34.Q5
  N440: J224.pin7, Register_34.Q6
  N441: J224.pin8, Register_34.Q7
  N442: J225.pin1, Register_33.Q3
  N443: J225.pin2, Register_33.Q2
  N444: J225.pin3, Register_33.Q1
  N445: J225.pin4, Register_33.Q0
  N446: J225.pin5, Register_33.Q4
  N447: J225.pin6, Register_33.Q5
  N448: J225.pin7, Register_33.Q6
  N449: J225.pin8, Register_33.Q7
  N450: J226.pin1, Register_35.Q3
  N451: J226.pin2, Register_35.Q2
  N452: J226.pin3, Register_35.Q1
  N453: J226.pin4, Register_35.Q0
  N454: J226.pin5, Register_35.Q4
  N455: J226.pin6, Register_35.Q5
  N456: J226.pin7, Register_35.Q6
  N457: J226.pin8, Register_35.Q7
  N458: J227.pin1, Register_36.Q3
  N459: J227.pin2, Register_36.Q2
  N460: J227.pin3, Register_36.Q1
  N461: J227.pin4, Register_36.Q0
  N462: J227.pin5, Register_36.Q4
  N463: J227.pin6, Register_36.Q5
  N464: J227.pin7, Register_36.Q6
  N465: J227.pin8, Register_36.Q7
  N466: J228.pin1, Register_37.Q3
  N467: J228.pin2, Register_37.Q2
  N468: J228.pin3, Register_37.Q1
  N469: J228.pin4, Register_37.Q0
  N470: J228.pin5, Register_37.Q4
  N471: J228.pin6, Register_37.Q5
  N472: J228.pin7, Register_37.Q6
  N473: J228.pin8, Register_37.Q7
  N474: J229.pin1, Register_38.Q3
  N475: J229.pin2, Register_38.Q2
  N476: J229.pin3, Register_38.Q1
  N477: J229.pin4, Register_38.Q0
  N478: J229.pin5, Register_38.Q4
  N479: J229.pin6, Register_38.Q5
  N480: J229.pin7, Register_38.Q6
  N481: J229.pin8, Register_38.Q7
  N482: J230.pin1, Register_39.Q3
  N483: J230.pin2, Register_39.Q2
  N484: J230.pin3, Register_39.Q1
  N485: J230.pin4, Register_39.Q0
  N486: J230.pin5, Register_39.Q4
  N487: J230.pin6, Register_39.Q5
  N488: J230.pin7, Register_39.Q6
  N489: J230.pin8, Register_39.Q7
  N490: J231.pin1, Register_40.Q3
  N491: J231.pin2, Register_40.Q2
  N492: J231.pin3, Register_40.Q1
  N493: J231.pin4, Register_40.Q0
  N494: J231.pin5, Register_40.Q4
  N495: J231.pin6, Register_40.Q5
  N496: J231.pin7, Register_40.Q6
  N497: J231.pin8, Register_40.Q7
  N498: Register_33.MR, Register_33.VCC
  N499: Register_33.SH_CP, Register_34.SH_CP, Register_35.SH_CP, Register_36.SH_CP, Register_37.SH_CP, Register_38.SH_CP, Register_39.SH_CP, Register_40.SH_CP
  N500: Register_33.ST_CP, Register_34.ST_CP, Register_35.ST_CP, Register_36.ST_CP, Register_37.ST_CP, Register_38.ST_CP, Register_39.ST_CP, Register_40.ST_CP
  N501: Register_33.DS, Register_35.Q7'
  N502: Register_34.Q7', Register_35.DS
  N503: Register_34.MR, Register_34.VCC
  N504: Register_34.DS, Register_36.Q7'
  N505: Register_35.MR, Register_35.VCC
  N506: Register_36.MR, Register_36.VCC
  N507: Register_36.DS, Register_37.Q7'
  N508: Register_37.MR, Register_37.VCC
  N509: Register_37.DS, Register_38.Q7'
  N510: Register_38.MR, Register_38.VCC
  N511: Register_38.DS, Register_39.Q7'
  N512: Register_39.MR, Register_39.VCC
  N513: Register_39.DS, Register_40.Q7'
  N514: Register_40.MR, Register_40.VCC
  N515: J232.pin1, Register_42.Q3
  N516: J232.pin2, Register_42.Q2
  N517: J232.pin3, Register_42.Q1
  N518: J232.pin4, Register_42.Q0
  N519: J232.pin5, Register_42.Q4
  N520: J232.pin6, Register_42.Q5
  N521: J232.pin7, Register_42.Q6
  N522: J232.pin8, Register_42.Q7
  N523: J233.pin1, Register_41.Q3
  N524: J233.pin2, Register_41.Q2
  N525: J233.pin3, Register_41.Q1
  N526: J233.pin4, Register_41.Q0
  N527: J233.pin5, Register_41.Q4
  N528: J233.pin6, Register_41.Q5
  N529: J233.pin7, Register_41.Q6
  N530: J233.pin8, Register_41.Q7
  N531: J234.pin1, Register_43.Q3
  N532: J234.pin2, Register_43.Q2
  N533: J234.pin3, Register_43.Q1
  N534: J234.pin4, Register_43.Q0
  N535: J234.pin5, Register_43.Q4
  N536: J234.pin6, Register_43.Q5
  N537: J234.pin7, Register_43.Q6
  N538: J234.pin8, Register_43.Q7
  N539: J235.pin1, Register_44.Q3
  N540: J235.pin2, Register_44.Q2
  N541: J235.pin3, Register_44.Q1
  N542: J235.pin4, Register_44.Q0
  N543: J235.pin5, Register_44.Q4
  N544: J235.pin6, Register_44.Q5
  N545: J235.pin7, Register_44.Q6
  N546: J235.pin8, Register_44.Q7
  N547: J236.pin1, Register_45.Q3
  N548: J236.pin2, Register_45.Q2
  N549: J236.pin3, Register_45.Q1
  N550: J236.pin4, Register_45.Q0
  N551: J236.pin5, Register_45.Q4
  N552: J236.pin6, Register_45.Q5
  N553: J236.pin7, Register_45.Q6
  N554: J236.pin8, Register_45.Q7
  N555: J237.pin1, Register_46.Q3
  N556: J237.pin2, Register_46.Q2
  N557: J237.pin3, Register_46.Q1
  N558: J237.pin4, Register_46.Q0
  N559: J237.pin5, Register_46.Q4
  N560: J237.pin6, Register_46.Q5
  N561: J237.pin7, Register_46.Q6
  N562: J237.pin8, Register_46.Q7
  N563: J238.pin1, Register_47.Q3
  N564: J238.pin2, Register_47.Q2
  N565: J238.pin3, Register_47.Q1
  N566: J238.pin4, Register_47.Q0
  N567: J238.pin5, Register_47.Q4
  N568: J238.pin6, Register_47.Q5
  N569: J238.pin7, Register_47.Q6
  N570: J238.pin8, Register_47.Q7
  N571: J239.pin1, Register_48.Q3
  N572: J239.pin2, Register_48.Q2
  N573: J239.pin3, Register_48.Q1
  N574: J239.pin4, Register_48.Q0
  N575: J239.pin5, Register_48.Q4
  N576: J239.pin6, Register_48.Q5
  N577: J239.pin7, Register_48.Q6
  N578: J239.pin8, Register_48.Q7
  N579: Register_41.MR, Register_41.VCC
  N580: Register_41.SH_CP, Register_42.SH_CP, Register_43.SH_CP, Register_44.SH_CP, Register_45.SH_CP, Register_46.SH_CP, Register_47.SH_CP, Register_48.SH_CP
  N581: Register_41.ST_CP, Register_42.ST_CP, Register_43.ST_CP, Register_44.ST_CP, Register_45.ST_CP, Register_46.ST_CP, Register_47.ST_CP, Register_48.ST_CP
  N582: Register_41.DS, Register_43.Q7'
  N583: Register_42.Q7', Register_43.DS
  N584: Register_42.MR, Register_42.VCC
  N585: Register_42.DS, Register_44.Q7'
  N586: Register_43.MR, Register_43.VCC
  N587: Register_44.MR, Register_44.VCC
  N588: Register_44.DS, Register_45.Q7'
  N589: Register_45.MR, Register_45.VCC
  N590: Register_45.DS, Register_46.Q7'
  N591: Register_46.MR, Register_46.VCC
  N592: Register_46.DS, Register_47.Q7'
  N593: Register_47.MR, Register_47.VCC
  N594: Register_47.DS, Register_48.Q7'
  N595: Register_48.MR, Register_48.VCC
  N596: J240.pin1, Register_51.Q3
  N597: J240.pin2, Register_51.Q2
  N598: J240.pin3, Register_51.Q1
  N599: J240.pin4, Register_51.Q0
  N600: J240.pin5, Register_51.Q4
  N601: J240.pin6, Register_51.Q5
  N602: J240.pin7, Register_51.Q6
  N603: J240.pin8, Register_51.Q7
  N604: J241.pin1, Register_52.Q3
  N605: J241.pin2, Register_52.Q2
  N606: J241.pin3, Register_52.Q1
  N607: J241.pin4, Register_52.Q0
  N608: J241.pin5, Register_52.Q4
  N609: J241.pin6, Register_52.Q5
  N610: J241.pin7, Register_52.Q6
  N611: J241.pin8, Register_52.Q7
  N612: J242.pin1, Register_49.Q3
  N613: J242.pin2, Register_49.Q2
  N614: J242.pin3, Register_49.Q1
  N615: J242.pin4, Register_49.Q0
  N616: J242.pin5, Register_49.Q4
  N617: J242.pin6, Register_49.Q5
  N618: J242.pin7, Register_49.Q6
  N619: J242.pin8, Register_49.Q7
  N620: J243.pin1, Register_50.Q3
  N621: J243.pin2, Register_50.Q2
  N622: J243.pin3, Register_50.Q1
  N623: J243.pin4, Register_50.Q0
  N624: J243.pin5, Register_50.Q4
  N625: J243.pin6, Register_50.Q5
  N626: J243.pin7, Register_50.Q6
  N627: J243.pin8, Register_50.Q7
  N628: J244.pin1, Register_53.Q3
  N629: J244.pin2, Register_53.Q2
  N630: J244.pin3, Register_53.Q1
  N631: J244.pin4, Register_53.Q0
  N632: J244.pin5, Register_53.Q4
  N633: J244.pin6, Register_53.Q5
  N634: J244.pin7, Register_53.Q6
  N635: J244.pin8, Register_53.Q7
  N636: J245.pin1, Register_54.Q3
  N637: J245.pin2, Register_54.Q2
  N638: J245.pin3, Register_54.Q1
  N639: J245.pin4, Register_54.Q0
  N640: J245.pin5, Register_54.Q4
  N641: J245.pin6, Register_54.Q5
  N642: J245.pin7, Register_54.Q6
  N643: J245.pin8, Register_54.Q7
  N644: J246.pin1, Register_55.Q3
  N645: J246.pin2, Register_55.Q2
  N646: J246.pin3, Register_55.Q1
  N647: J246.pin4, Register_55.Q0
  N648: J246.pin5, Register_55.Q4
  N649: J246.pin6, Register_55.Q5
  N650: J246.pin7, Register_55.Q6
  N651: J246.pin8, Register_55.Q7
  N652: J247.pin1, Register_56.Q3
  N653: J247.pin2, Register_56.Q2
  N654: J247.pin3, Register_56.Q1
  N655: J247.pin4, Register_56.Q0
  N656: J247.pin5, Register_56.Q4
  N657: J247.pin6, Register_56.Q5
  N658: J247.pin7, Register_56.Q6
  N659: J247.pin8, Register_56.Q7
  N660: J248.pin1, Register_57.Q3
  N661: J248.pin2, Register_57.Q2
  N662: J248.pin3, Register_57.Q1
  N663: J248.pin4, Register_57.Q0
  N664: J248.pin5, Register_57.Q4
  N665: J248.pin6, Register_57.Q5
  N666: J248.pin7, Register_57.Q6
  N667: J248.pin8, Register_57.Q7
  N668: J249.pin1, Register_58.Q3
  N669: J249.pin2, Register_58.Q2
  N670: J249.pin3, Register_58.Q1
  N671: J249.pin4, Register_58.Q0
  N672: J249.pin5, Register_58.Q4
  N673: J249.pin6, Register_58.Q5
  N674: J249.pin7, Register_58.Q6
  N675: J249.pin8, Register_58.Q7
  N676: J250.pin1, Register_59.Q3
  N677: J250.pin2, Register_59.Q2
  N678: J250.pin3, Register_59.Q1
  N679: J250.pin4, Register_59.Q0
  N680: J250.pin5, Register_59.Q4
  N681: J250.pin6, Register_59.Q5
  N682: J250.pin7, Register_59.Q6
  N683: J250.pin8, Register_59.Q7
  N684: J251.pin1, Register_60.Q3
  N685: J251.pin2, Register_60.Q2
  N686: J251.pin3, Register_60.Q1
  N687: J251.pin4, Register_60.Q0
  N688: J251.pin5, Register_60.Q4
  N689: J251.pin6, Register_60.Q5
  N690: J251.pin7, Register_60.Q6
  N691: J251.pin8, Register_60.Q7
  N692: J252.pin1, Register_61.Q3
  N693: J252.pin2, Register_61.Q2
  N694: J252.pin3, Register_61.Q1
  N695: J252.pin4, Register_61.Q0
  N696: J252.pin5, Register_61.Q4
  N697: J252.pin6, Register_61.Q5
  N698: J252.pin7, Register_61.Q6
  N699: J252.pin8, Register_61.Q7
  N700: J253.pin1, Register_62.Q3
  N701: J253.pin2, Register_62.Q2
  N702: J253.pin3, Register_62.Q1
  N703: J253.pin4, Register_62.Q0
  N704: J253.pin5, Register_62.Q4
  N705: J253.pin6, Register_62.Q5
  N706: J253.pin7, Register_62.Q6
  N707: J253.pin8, Register_62.Q7
  N708: J254.pin1, Register_63.Q3
  N709: J254.pin2, Register_63.Q2
  N710: J254.pin3, Register_63.Q1
  N711: J254.pin4, Register_63.Q0
  N712: J254.pin5, Register_63.Q4
  N713: J254.pin6, Register_63.Q5
  N714: J254.pin7, Register_63.Q6
  N715: J254.pin8, Register_63.Q7
  N716: J255.pin1, Register_64.Q3
  N717: J255.pin2, Register_64.Q2
  N718: J255.pin3, Register_64.Q1
  N719: J255.pin4, Register_64.Q0
  N720: J255.pin5, Register_64.Q4
  N721: J255.pin6, Register_64.Q5
  N722: J255.pin7, Register_64.Q6
  N723: J255.pin8, Register_64.Q7
  N724: Register_49.MR, Register_49.VCC
  N725: Register_49.SH_CP, Register_51.SH_CP, Register_53.SH_CP, Register_55.SH_CP, Register_57.SH_CP, Register_59.SH_CP, Register_61.SH_CP, Register_63.SH_CP
  N726: Register_49.ST_CP, Register_51.ST_CP, Register_53.ST_CP, Register_55.ST_CP, Register_57.ST_CP, Register_59.ST_CP, Register_61.ST_CP, Register_63.ST_CP
  N727: Register_49.DS, Register_53.Q7'
  N728: Register_50.MR, Register_50.VCC
  N729: Register_50.SH_CP, Register_52.SH_CP, Register_54.SH_CP, Register_56.SH_CP, Register_58.SH_CP, Register_60.SH_CP, Register_62.SH_CP, Register_64.SH_CP
  N730: Register_50.ST_CP, Register_52.ST_CP, Register_54.ST_CP, Register_56.ST_CP, Register_58.ST_CP, Register_60.ST_CP, Register_62.ST_CP, Register_64.ST_CP
  N731: Register_50.DS, Register_54.Q7'
  N732: Register_51.Q7', Register_53.DS
  N733: Register_51.MR, Register_51.VCC
  N734: Register_51.DS, Register_55.Q7'
  N735: Register_52.Q7', Register_54.DS
  N736: Register_52.MR, Register_52.VCC
  N737: Register_52.DS, Register_56.Q7'
  N738: Register_53.MR, Register_53.VCC
  N739: Register_54.MR, Register_54.VCC
  N740: Register_55.MR, Register_55.VCC
  N741: Register_55.DS, Register_57.Q7'
  N742: Register_56.MR, Register_56.VCC
  N743: Register_56.DS, Register_58.Q7'
  N744: Register_57.MR, Register_57.VCC
  N745: Register_57.DS, Register_59.Q7'
  N746: Register_58.MR, Register_58.VCC
  N747: Register_58.DS, Register_60.Q7'
  N748: Register_59.MR, Register_59.VCC
  N749: Register_59.DS, Register_61.Q7'
  N750: Register_60.MR, Register_60.VCC
  N751: Register_60.DS, Register_62.Q7'
  N752: Register_61.MR, Register_61.VCC
  N753: Register_61.DS, Register_63.Q7'
  N754: Register_62.MR, Register_62.VCC
  N755: Register_62.DS, Register_64.Q7'
  N756: Register_63.MR, Register_63.VCC
  N757: Register_64.MR, Register_64.VCC

notes:
  Electrorchestrion - Organic
  Copyright 2020 Gabriel Peressini
  All rights reserved.
  1
  8
  4
  5
